# Fritzing sketch motion (saved by Fritzing 0.9.3b)
breadboards: 1

parts:
  Raspberry_Pi_1 = Raspberry Pi 3 [part_number=RPI-3-V1.2]
  PIR1 = PIR sensor

nets:
  3V3: Raspberry_Pi_1.3v3, PIR1.VDD
  N1: Raspberry_Pi_1.GPIO4, PIR1.SIG
  GND: Raspberry_Pi_1.GND, PIR1.GND
