# Fritzing sketch temp_humidity (saved by Fritzing 0.9.3b)
breadboards: 1

parts:
  Raspberry_Pi_1 = Raspberry Pi 3 [part_number=RPI-3-V1.2]
  DHT1 = DHT22 Humidity and Temperature Sensor
  R1 = Resistor [tolerance=±5% resistance=220 package=THT]

nets:
  N1: Raspberry_Pi_1.GPIO4, DHT1.DATA, R1.Pin_1
  GND: Raspberry_Pi_1.GND, DHT1.GND
  5V: Raspberry_Pi_1.5V, DHT1.VDD, R1.Pin_0
